# Fritzing sketch scheme (saved by Fritzing 0.9.9b)

parts:
  MotorShield = Arduino Motor Shield (Rev3)
  HC-SR04_Sensor_1 = HC-SR04 Ultrasonic Distance Sensor
  HC-SR04_Sensor_3 = HC-SR04 Ultrasonic Distance Sensor
  HC-SR04_Sensor_4 = HC-SR04 Ultrasonic Distance Sensor
  HC-SR04_Sensor_2 = HC-SR04 Ultrasonic Distance Sensor

nets:
  GND: MotorShield.GND, HC-SR04_Sensor_1.GND, HC-SR04_Sensor_3.GND, HC-SR04_Sensor_4.GND, HC-SR04_Sensor_2.GND
  VCC: MotorShield.5V, HC-SR04_Sensor_1.VCC, HC-SR04_Sensor_3.VCC, HC-SR04_Sensor_4.VCC, HC-SR04_Sensor_2.VCC
  N1: MotorShield.D10_PWM, HC-SR04_Sensor_3.ECHO
  N2: MotorShield.D11_PWM/B, HC-SR04_Sensor_1.ECHO
  N3: MotorShield.D12/DirA, HC-SR04_Sensor_1.TRIG
  N4: MotorShield.D13/DirB, HC-SR04_Sensor_3.TRIG
  N5: MotorShield.D4, HC-SR04_Sensor_2.TRIG
  N6: MotorShield.D6_PWM, HC-SR04_Sensor_4.ECHO
  N7: MotorShield.D7, HC-SR04_Sensor_4.TRIG
  N8: MotorShield.D5_PWM, HC-SR04_Sensor_2.ECHO
